# Fritzing sketch Schema_circuito_dispenser (saved by Fritzing 0.9.4)
breadboards: 1

parts:
  Arduino = Arduino Uno (Rev3) - ICSP
  ESP32_-_Back1 = ESP32 - CAM
  J1 = Basic Servo
  S1 = Pushbutton [package="[THT]"]
  R1 = Resistor [tolerance=±5% resistance=220 package=THT]
  LED1 = smd LED [color="Red (633nm)" package="0603 [SMD]"]
  R2 = Resistor [tolerance=±5% resistance=220 package="1206 [SMD]"]

nets:
  N1: Arduino.D9_PWM, J1.pulse
  N2: Arduino.D13/SCK, R2.Pin_1
  GND: Arduino.GND, ESP32_-_Back1.GND#7, J1.gnd, R1.Pin_1, LED1.cathode
  N3: Arduino.D2, ESP32_-_Back1.GPIO1_/_TX
  N4: Arduino.D3_PWM, ESP32_-_Back1.GND#16
  N5: Arduino.D7, S1.Pin_1, S1.Pin_2, R1.Pin_0
  3V3: Arduino.3V3, J1.vcc, S1.Pin_3, S1.Pin_4
  5V: Arduino.5V, ESP32_-_Back1.5V
  N6: LED1.anode, R2.Pin_0

custom parts:
  ESP32 - CAM: The ESP32-CAM has a very competitive small-size camera module that can operate independently as a minimum system with a footprint of only 27*40.5*4.5mm and a deep sleep current of up to 6mA.
